// Logisim project project.circ as structural Verilog: 1 circuit, main circuit main
module main (
);

  wire clock_1_out, comparator_1_eq, pc_carry, pull_resistor_1_node, pull_resistor_2_node,
       pull_resistor_3_node, pull_resistor_4_node, RESET_out, STEP_out;
  wire [3:0] REG_A_q, REG_A_q_2, REG_B_q, REG_B_q_2, REG_C_q, REG_C_q_2;
  wire [7:0] prog_data, undriven, undriven_2, undriven_3;
  wire [9:8] counter_1_q;
  wire [15:0] pc_q;

  Clock clock_1 (.out(clock_1_out));
  Pull_Resistor pull_resistor_1 (.node(pull_resistor_1_node));
  buf buffer_1 (pull_resistor_1_node, clock_1_out);
  buf buffer_2 (pull_resistor_1_node, STEP_out);
  Counter #(.max('h3), .width(2)) counter_1 (
    .clr(RESET_out), .clk(pull_resistor_1_node), .D(2'b00), .Q(counter_1_q));  // open: load, up, count, carry
  Button RESET (.out(RESET_out));
  Comparator #(.width(2)) comparator_1 (.a(2'b00), .b(counter_1_q), .eq(comparator_1_eq));  // open: gt, lt
  Counter #(.max('hffff), .width(16)) pc (
    .clr(RESET_out), .clk(comparator_1_eq), .carry(pc_carry), .Q(pc_q));  // open: load, up, count, D
  LED overflow (.in(pc_carry));
  Button STEP (.out(STEP_out));
  ROM #(.addrWidth(16)) prog (.addr(pc_q), .data(prog_data));
  Hex_Digit_Display hex_digit_display_1 (.value(REG_A_q_2));  // open: dp
  Hex_Digit_Display hex_digit_display_2 (.value(REG_B_q_2));  // open: dp
  Hex_Digit_Display hex_digit_display_3 (.value(REG_C_q_2));  // open: dp
  Hex_Digit_Display hex_digit_display_4 (.value(REG_A_q));  // open: dp
  Hex_Digit_Display hex_digit_display_5 (.value(REG_B_q));  // open: dp
  Hex_Digit_Display hex_digit_display_6 (.value(REG_C_q));  // open: dp
  Register REG_A (.D(undriven), .clk(pull_resistor_2_node), .Q({REG_A_q_2, REG_A_q}), .clr(RESET_out));  // open: en
  LED led_1 (.in(pull_resistor_2_node));
  Register REG_B (.D(undriven_2), .clk(pull_resistor_3_node), .Q({REG_B_q_2, REG_B_q}), .clr(RESET_out));  // open: en
  LED led_2 (.in(pull_resistor_3_node));
  Register REG_C (.D(undriven_3), .clk(pull_resistor_4_node), .Q({REG_C_q_2, REG_C_q}), .clr(RESET_out));  // open: en
  LED led_3 (.in(pull_resistor_4_node));
  Pull_Resistor pull_resistor_2 (.node(pull_resistor_2_node));
  Pull_Resistor pull_resistor_3 (.node(pull_resistor_3_node));
  Pull_Resistor pull_resistor_4 (.node(pull_resistor_4_node));
  Hex_Digit_Display hex_digit_display_7 (.value(prog_data[7:4]));  // open: dp
  Hex_Digit_Display hex_digit_display_8 (.value(prog_data[3:0]));  // open: dp
  ROM #(.addrWidth(16), .dataWidth(4)) rom_1 (.addr({counter_1_q, prog_data, {6{1'b0}}}));  // open: data

  // Notes on the sheet:
  //   buffer_1 drives only 1 and floats otherwise
  //   buffer_2 drives only 1 and floats otherwise
  //   contents of prog (hex, n*v repeats v):
  //   8*2 88*1
  //   contents of rom_1 (hex, n*v repeats v):
  //   16*f
endmodule
